// Logisim project group5_project.circ as structural Verilog: 1 circuit, main circuit main
module main (
  input  KEY,
  input  HELMET_DETECTED,
  input  HELMET_TYPE,
  input  STRAP_LOCKED,
  output START_BLOCKED,
  output ALLOW
);

  wire and_1_out, and_2_out, and_3_out, and_5_out, and_6_out, clock_1_out, D0_q, D1_q, D2_q, or_1_out,
       or_2_out, or_3_out;

  Clock clock_1 (.out(clock_1_out));
  D_Flip_Flop D2 (.clk(clock_1_out), .D(or_1_out), .Q(D2_q));  // open: Qn, preset, en, reset
  D_Flip_Flop D1 (.clk(clock_1_out), .D(or_2_out), .Q(D1_q));  // open: Qn, preset, en, reset
  D_Flip_Flop D0 (.clk(clock_1_out), .D(or_3_out), .Q(D0_q));  // open: Qn, preset, en, reset
  and and_1 (and_1_out, HELMET_TYPE, HELMET_DETECTED, KEY, ~D2_q, D1_q, D0_q);  // AND_Gate
  and and_2 (and_2_out, HELMET_TYPE, ~D0_q, ~D1_q, ~D2_q);  // AND_Gate
  and and_3 (and_3_out, ~D0_q, D1_q, ~D2_q, KEY, HELMET_DETECTED, HELMET_TYPE);  // AND_Gate
  and and_4 (ALLOW, ~D0_q, ~D1_q, D2_q, KEY, HELMET_DETECTED, HELMET_TYPE, STRAP_LOCKED);  // AND_Gate
  and and_5 (and_5_out, HELMET_DETECTED, KEY, ~D2_q, ~D1_q, D0_q);  // AND_Gate
  and and_6 (and_6_out, HELMET_TYPE, HELMET_DETECTED, KEY, ~D2_q, D1_q, ~D0_q);  // AND_Gate
  and and_7 (START_BLOCKED, ~STRAP_LOCKED, HELMET_TYPE, HELMET_DETECTED, KEY, D2_q, ~D1_q, ~D0_q);  // AND_Gate
  or or_1 (or_1_out, and_1_out, ALLOW, START_BLOCKED);
  or or_2 (or_2_out, START_BLOCKED, and_5_out, and_6_out);
  or or_3 (or_3_out, and_2_out, and_3_out, ALLOW);
endmodule
